// Logisim project EBP1.circ as structural Verilog
module DLatch (
  input  D,
  input  En,
  output Q
);

  wire and_1_out, and_2_out, nor_1_out, not_1_out;

  not not_1 (not_1_out, D);
  and and_1 (and_1_out, not_1_out, En);
  and and_2 (and_2_out, En, D);
  nor nor_1 (nor_1_out, and_1_out, Q);
  nor nor_2 (Q, nor_1_out, and_2_out);
endmodule
